// Logisim project 201811970.circ as structural Verilog: 1 circuit, main circuit main
module main (
  input  x,
  input  y,
  output S,
  output Q_prime
);

  wire and_1_out, and_2_out, clock_1_out, nand_2_out, nand_3_out, nand_4_out, nand_5_out, nand_6_out,
       or_1_out, xor_1_out;

  and and_1 (and_1_out, x, y);
  nand nand_1 (Q_prime, nand_4_out, nand_2_out);
  nand nand_2 (nand_2_out, Q_prime, nand_5_out);
  xor xor_1 (xor_1_out, x, y);
  and and_2 (and_2_out, xor_1_out, nand_2_out);
  xor xor_2 (S, xor_1_out, nand_2_out);
  nand nand_3 (nand_3_out, or_1_out, nand_4_out);
  nand nand_4 (nand_4_out, nand_3_out, clock_1_out, nand_5_out);
  nand nand_5 (nand_5_out, clock_1_out, nand_6_out);
  nand nand_6 (nand_6_out, nand_5_out, nand_3_out);
  or or_1 (or_1_out, and_2_out, and_1_out);
  Clock clock_1 (.out(clock_1_out));
endmodule
